// Logisim project CPU.circ as structural Verilog: 1 circuit, main circuit CPU
module CPU (
  input  rst
);

  wire ALUsrc, and_1_out, and_2_out, Branch, branch_1_isbranch, clock_1_out, clock_2_out, dm_1_p4, DM_ext,
       EXTop, JmpLnk, JmpSrc, Jump, MemtoReg, MemWrite, negaflg, RegWrite, zeroflg;
  wire [1:0] DM_size, RegDst;
  wire [2:0] NPCop;
  wire [3:0] ALUop, BRop;
  wire [4:0] GRF_A1, GRF_A2, GRF_A3, rd, shamt;
  wire [5:0] funct, op;
  wire [15:0] imm;
  wire [25:0] addr;
  wire [31:0] ALUresult, ALUsrcA, ALUsrcB, DM_RD, DM_WD, ExtImm, GRF_WD, im_1_rd, multiplexer_2_out, nextPC,
       PC, PC_4;

  Clock clock_1 (.out(clock_1_out));
  PC pc_1 (.nextPC(nextPC), .PC(PC), .clk(clock_1_out), .rst(rst));
  EXT ext_1 (.in(imm), .EXTop(EXTop), .out(ExtImm));
  Branch branch_1 (.branchop(BRop), .ALUzero(zeroflg), .ALUnega(negaflg), .isBranch(branch_1_isbranch));
  and and_1 (and_1_out, Jump, ~JmpSrc);  // AND_Gate
  and and_2 (and_2_out, Jump, JmpSrc);
  NPC npc_1 (.PC(PC), .imm16(imm), .addr26(addr), .ra32(ALUsrcA), .op(NPCop), .nextPC(nextPC), .PC4(PC_4));
  Priority_Encoder priority_encoder_1 (
    .in0(1'b1), .in1(branch_1_isbranch), .in2(and_1_out), .in3(and_2_out), .out(NPCop));  // open: in4, in5, in6, in7, en_in, gs, en_out
  IF if_1 (
    .Instr(im_1_rd), .op(op), .rs(GRF_A1), .rt(GRF_A2), .rd(rd), .shamt(shamt), .funct(funct), .imm(imm),
    .addr(addr));
  IM im_1 (.A(PC), .RD(im_1_rd));
  ALU alu_1 (.A(ALUsrcA), .B(ALUsrcB), .Op(ALUop), .Out(ALUresult), .zero(zeroflg), .nega(negaflg));
  Multiplexer #(.width(32), .disabled(0), .enable("false")) multiplexer_1 (
    .in0(DM_WD), .in1(ExtImm), .out(ALUsrcB), .sel(ALUsrc));
  Multiplexer #(.width(32), .disabled(0), .enable("false")) multiplexer_2 (
    .in0(ALUresult), .in1(DM_RD), .out(multiplexer_2_out), .sel(MemtoReg));
  GRF grf_1 (
    .A1(GRF_A1), .A2(GRF_A2), .A3(GRF_A3), .WD(GRF_WD), .RD1(ALUsrcA), .RD2(DM_WD), .clk(clock_2_out),
    .reset(rst), .WE(RegWrite));
  Clock clock_2 (.out(clock_2_out));
  Multiplexer #(.select(2), .width(5), .disabled(0), .enable("false")) multiplexer_3 (
    .in0(rd), .in1(GRF_A2), .in2({5{1'b1}}), .out(GRF_A3), .sel(RegDst));  // open: in3
  Multiplexer #(.width(32), .disabled(0), .enable("false")) multiplexer_4 (
    .in0(multiplexer_2_out), .in1(PC_4), .out(GRF_WD), .sel(JmpLnk));
  // DM dm_1: pin names not known; wires that end beside it: ALUresult, DM_WD, DM_size, dm_1_p4, MemWrite, DM_ext, rst, DM_RD
  Clock clock_3 (.out(dm_1_p4));
  Control control_1 (
    .opcode(op), .funct(funct), .MemtoReg(MemtoReg), .MemWrite(MemWrite), .ALUop(ALUop), .EXTop(EXTop),
    .ALUsrc(ALUsrc), .RegDst(RegDst), .RegWrite(RegWrite), .BRop(BRop), .Jump(Jump), .JmpSrc(JmpSrc),
    .JmpLnk(JmpLnk), .Branch(Branch), .Msize(DM_size), .Mext(DM_ext), .rs(GRF_A1), .rt(GRF_A2));  // open: Shift, SHop, SHsrc

  // Other names for the same wires on the sheet: DM_A[31:0] = ALUresult; GRF_RD1[31:0] = ALUsrcA;
  //   GRF_RD2[31:0] = DM_WD; rs[4:0] = GRF_A1; rt[4:0] = GRF_A2
endmodule
